// Logisim project arquitetura_de_computadores_16_05_2024.circ as structural Verilog: 16 circuits, main circuit main
module main (
  output [7:0] out_1
);

  wire clock_1_out, not_1_out, not_2_out, Overflow_q, Reset_out, uc_1_clk_ac, uc_1_clk_pc, uc_1_clk_ram,
       uc_1_clk_rl, \uc_1_direção , uc_1_e, uc_1_load, uc_1_r_w, uc_1_rst_pc, ula_1_overflow,
       ula_1_overflow_2, Zero_q;
  wire [2:0] \uc_1_operação ;
  wire [3:0] mux_1_s, PC_q, ram_2_data, reg_ac_1_d_2, \uc_1_barr__endereços , uc_1_dados, uc_1_operando,
       ula_1_out_6;
  wire [7:0] ir_1_q;

  Counter #(.width(4), .max('hf), .trigger("falling")) PC (
    .load(uc_1_load), .D(uc_1_dados), .count(not_1_out), .Q(PC_q), .clk(uc_1_clk_pc), .clr(uc_1_rst_pc));  // open: carry
  not not_1 (not_1_out, uc_1_load);
  UC uc_1 (
    .\Barr__Endereços (\uc_1_barr__endereços ), .Operando(uc_1_operando), .\Direção (\uc_1_direção ),
    .E(uc_1_e), .\Operação (\uc_1_operação ), .\Instrução (ir_1_q), .Clock(clock_1_out), .Reset(Reset_out),
    .Rst_PC(uc_1_rst_pc), .clk_Rl(uc_1_clk_rl), .clk_AC(uc_1_clk_ac), .clk_PC(uc_1_clk_pc),
    .clk_RAM(uc_1_clk_ram), .Overflow(Overflow_q), .Zero(Zero_q), .Dados(uc_1_dados), .Load(uc_1_load),
    .R_W(uc_1_r_w));
  Clock clock_1 (.out(clock_1_out));
  RAM #(.addrWidth(4)) ram_1 (.addr(PC_q), .data(out_1));  // open: sel, clk, ld, clr
  Button Reset (.out(Reset_out));
  IR ir_1 (.D(out_1), .Clock(uc_1_clk_rl), .Q(ir_1_q));
  // Probe on ir_1_q
  MUX mux_1 (.in_3(uc_1_e), .S(mux_1_s), .E(uc_1_operando), .D(ram_2_data));
  // Probe on reg_ac_1_d_2
  ULA ula_1 (
    .D(\uc_1_direção ), .A(reg_ac_1_d_2), .B(mux_1_s), .in_4(\uc_1_operação ), .Overflow(ula_1_overflow),
    .Overflow_2(ula_1_overflow_2), .out_6(ula_1_out_6));
  REG_AC reg_ac_1 (.D(ula_1_out_6), .Clock(uc_1_clk_ac), .D_2(reg_ac_1_d_2));
  // Probe on mux_1_s
  D_Flip_Flop Overflow (.clk(uc_1_clk_ac), .D(ula_1_overflow), .Q(Overflow_q));  // open: Qn, preset, en, reset
  D_Flip_Flop Zero (.clk(uc_1_clk_ac), .D(ula_1_overflow_2), .Q(Zero_q));  // open: Qn, preset, en, reset
  // Probe on reg_ac_1_d_2
  RAM #(.addrWidth(4), .dataWidth(4)) ram_2 (
    .addr(\uc_1_barr__endereços ), .data(ram_2_data), .clk(uc_1_clk_ram), .ld(uc_1_r_w));  // open: sel, clr
  not not_2 (not_2_out, uc_1_r_w);
  BUFFER buffer_1 (.in_2(not_2_out), .B(reg_ac_1_d_2), .S(ram_2_data));
endmodule

module AD_1 (
  input  A,
  input  B,
  input  Vem_1,
  output S,
  output Vai_1
);

  wire and_1_out, and_2_out, or_1_out, xor_1_out;

  xor xor_1 (xor_1_out, A, B);
  or or_1 (or_1_out, Vem_1, B);
  and and_1 (and_1_out, Vem_1, B);
  xor xor_2 (S, xor_1_out, Vem_1);
  and and_2 (and_2_out, or_1_out, A);
  or or_2 (Vai_1, and_2_out, and_1_out);
endmodule

module AD_4 (
  input  [3:0] in_1,
  input  [3:0] in_2,
  input  in_3,
  output out_4,
  output [3:0] out_5
);

  wire ad_1_2_vai_1, ad_1_3_vai_1, ad_1_4_vai_1;

  AD_1 ad_1_1 (.A(in_2[3]), .B(in_1[3]), .S(out_5[3]), .Vem_1(ad_1_2_vai_1), .Vai_1(out_4));
  AD_1 ad_1_2 (.A(in_2[2]), .B(in_1[2]), .S(out_5[2]), .Vem_1(ad_1_4_vai_1), .Vai_1(ad_1_2_vai_1));
  AD_1 ad_1_3 (.A(in_2[0]), .B(in_1[0]), .S(out_5[0]), .Vem_1(in_3), .Vai_1(ad_1_3_vai_1));
  AD_1 ad_1_4 (.A(in_2[1]), .B(in_1[1]), .S(out_5[1]), .Vem_1(ad_1_3_vai_1), .Vai_1(ad_1_4_vai_1));
endmodule

module SUB_1 (
  input  A,
  input  B,
  input  Vem_1,
  output S,
  output Vai_1
);

  wire and_1_out, and_2_out, not_1_out, or_1_out, xor_1_out;

  not not_1 (not_1_out, A);
  xor xor_1 (xor_1_out, A, B);
  or or_1 (or_1_out, Vem_1, B);
  and and_1 (and_1_out, Vem_1, B);
  xor xor_2 (S, xor_1_out, Vem_1);
  and and_2 (and_2_out, or_1_out, not_1_out);
  or or_2 (Vai_1, and_2_out, and_1_out);
endmodule

module SUB_4 (
  input  [3:0] in_1,
  input  [3:0] in_2,
  input  in_3,
  output out_4,
  output [3:0] out_5
);

  wire sub_1_2_vai_1, sub_1_3_vai_1, sub_1_4_vai_1;

  SUB_1 sub_1_1 (.A(in_2[3]), .B(in_1[3]), .Vem_1(sub_1_2_vai_1), .S(out_5[3]), .Vai_1(out_4));
  SUB_1 sub_1_2 (.A(in_2[2]), .B(in_1[2]), .Vem_1(sub_1_4_vai_1), .S(out_5[2]), .Vai_1(sub_1_2_vai_1));
  SUB_1 sub_1_3 (.A(in_2[0]), .B(in_1[0]), .Vem_1(in_3), .S(out_5[0]), .Vai_1(sub_1_3_vai_1));
  SUB_1 sub_1_4 (.A(in_2[1]), .B(in_1[1]), .Vem_1(sub_1_3_vai_1), .S(out_5[1]), .Vai_1(sub_1_4_vai_1));
endmodule

module BUFFER (
  input  [3:0] B,
  input  in_2,
  output [3:0] S
);

  assign S[3] = in_2 ? B[3] : 1'bz;  // Controlled_Buffer controlled_buffer_1
  assign S[2] = in_2 ? B[2] : 1'bz;  // Controlled_Buffer controlled_buffer_2
  assign S[1] = in_2 ? B[1] : 1'bz;  // Controlled_Buffer controlled_buffer_3
  assign S[0] = in_2 ? B[0] : 1'bz;  // Controlled_Buffer controlled_buffer_4
endmodule

module BUFFER_CONTROLADO_INVERTIDO (
  input  [3:0] B,
  input  in_2,
  output [3:0] S
);

  assign S[2] = in_2 ? ~B[2] : 1'bz;  // Controlled_Inverter controlled_inverter_1
  assign S[3] = in_2 ? ~B[3] : 1'bz;  // Controlled_Inverter controlled_inverter_2
  assign S[0] = in_2 ? ~B[0] : 1'bz;  // Controlled_Inverter controlled_inverter_3
  assign S[1] = in_2 ? ~B[1] : 1'bz;  // Controlled_Inverter controlled_inverter_4
endmodule

module DECODER_3x8 (
  input  [2:0] in_1,
  output S0,
  output S1,
  output S2,
  output S3,
  output S4,
  output S5,
  output S6,
  output S7
);

  wire not_1_out, not_2_out, not_3_out, not_4_out, not_5_out, not_6_out, not_7_out, not_8_out, not_9_out,
       not_10_out, not_11_out, not_12_out;

  not not_1 (not_1_out, in_1[2]);
  not not_2 (not_2_out, in_1[1]);
  not not_3 (not_3_out, in_1[0]);
  not not_4 (not_4_out, in_1[2]);
  not not_5 (not_5_out, in_1[1]);
  not not_6 (not_6_out, in_1[2]);
  not not_7 (not_7_out, in_1[0]);
  not not_8 (not_8_out, in_1[2]);
  not not_9 (not_9_out, in_1[1]);
  not not_10 (not_10_out, in_1[0]);
  not not_11 (not_11_out, in_1[1]);
  not not_12 (not_12_out, in_1[0]);
  and and_1 (S7, in_1[2], in_1[1], in_1[0]);
  and and_2 (S0, not_1_out, not_2_out, not_3_out);
  and and_3 (S1, not_4_out, not_5_out, in_1[0]);
  and and_4 (S2, not_6_out, in_1[1], not_7_out);
  and and_5 (S3, not_8_out, in_1[1], in_1[0]);
  and and_6 (S4, in_1[2], not_9_out, not_10_out);
  and and_7 (S5, in_1[2], not_11_out, in_1[0]);
  and and_8 (S6, in_1[2], in_1[1], not_12_out);
endmodule

module ROT_L (
  input  [3:0] ABCD,
  input  [1:0] XY,
  output [3:0] abcd_2
);

  wire and_1_out, and_2_out, and_3_out, and_4_out, and_5_out, and_6_out, and_7_out, and_8_out, and_9_out;

  and and_1 (and_1_out, ~XY[1], ~XY[0], ABCD[3]);  // AND_Gate
  and and_2 (and_2_out, ~XY[1], XY[0], ABCD[2]);  // AND_Gate
  and and_3 (and_3_out, XY[1], ~XY[0], ABCD[1]);  // AND_Gate
  and and_4 (and_4_out, XY[1], XY[0], ABCD[0]);
  and and_5 (and_5_out, ~XY[1], ~XY[0], ABCD[2]);  // AND_Gate
  and and_6 (and_6_out, ~XY[1], XY[0], ABCD[1]);  // AND_Gate
  and and_7 (and_7_out, XY[1], ~XY[0], ABCD[0]);  // AND_Gate
  and and_8 (and_8_out, ~XY[1], ~XY[0], ABCD[1]);  // AND_Gate
  and and_9 (and_9_out, ~XY[1], XY[0], ABCD[0]);  // AND_Gate
  and and_10 (abcd_2[0], ~XY[1], ~XY[0], ABCD[0]);  // AND_Gate
  or or_1 (abcd_2[3], and_1_out, and_2_out, and_3_out, and_4_out);
  or or_2 (abcd_2[2], and_5_out, and_6_out, and_7_out);
  or or_3 (abcd_2[1], and_8_out, and_9_out);
endmodule

module ROT_W (
  input  [3:0] ABCD,
  input  [1:0] XY,
  output [3:0] abcd_2
);

  wire and_1_out, and_2_out, and_3_out, and_4_out, and_5_out, and_6_out, and_7_out, and_8_out, and_9_out;

  and and_1 (and_1_out, ~XY[1], ~XY[0], ABCD[0]);  // AND_Gate
  and and_2 (and_2_out, ~XY[1], XY[0], ABCD[1]);  // AND_Gate
  and and_3 (and_3_out, XY[1], ~XY[0], ABCD[2]);  // AND_Gate
  and and_4 (and_4_out, XY[1], XY[0], ABCD[3]);
  and and_5 (and_5_out, ~XY[1], ~XY[0], ABCD[1]);  // AND_Gate
  and and_6 (and_6_out, ~XY[1], XY[0], ABCD[2]);  // AND_Gate
  and and_7 (and_7_out, XY[1], ~XY[0], ABCD[3]);  // AND_Gate
  and and_8 (and_8_out, ~XY[1], ~XY[0], ABCD[2]);  // AND_Gate
  and and_9 (and_9_out, ~XY[1], XY[0], ABCD[3]);  // AND_Gate
  and and_10 (abcd_2[3], ~XY[1], ~XY[0], ABCD[3]);  // AND_Gate
  or or_1 (abcd_2[0], and_1_out, and_2_out, and_3_out, and_4_out);
  or or_2 (abcd_2[1], and_5_out, and_6_out, and_7_out);
  or or_3 (abcd_2[2], and_8_out, and_9_out);
endmodule

module OR (
  input  [3:0] A,
  input  [3:0] B,
  output [3:0] S
);

  or or_1 (S[3], A[3], B[3]);
  or or_2 (S[2], A[2], B[2]);
  or or_3 (S[1], A[1], B[1]);
  or or_4 (S[0], A[0], B[0]);
endmodule

module ULA (
  input  D,
  input  [3:0] A,
  input  [3:0] B,
  input  [2:0] in_4,
  output Overflow,
  output [3:0] out_6,
  output Overflow_2
);

  wire ad_4_1_out_4, and_1_out, and_2_out, decoder_3x8_1_s0, decoder_3x8_1_s1, decoder_3x8_1_s2,
       decoder_3x8_1_s3, decoder_3x8_1_s4, decoder_3x8_1_s5, decoder_3x8_1_s6, decoder_3x8_1_s7, not_1_out,
       sub_4_1_out_4;
  wire [3:0] ad_4_1_out_5, buffer_5_s, or_2_s, rot_l_1_abcd_2, rot_w_1_abcd_2, sub_4_1_out_5;

  or or_1 (Overflow, and_1_out, and_2_out);
  and and_1 (and_1_out, ad_4_1_out_4, decoder_3x8_1_s1);
  and and_2 (and_2_out, sub_4_1_out_4, decoder_3x8_1_s2);
  DECODER_3x8 decoder_3x8_1 (
    .S0(decoder_3x8_1_s0), .S1(decoder_3x8_1_s1), .S2(decoder_3x8_1_s2), .S3(decoder_3x8_1_s3),
    .S4(decoder_3x8_1_s4), .S5(decoder_3x8_1_s5), .S6(decoder_3x8_1_s6), .S7(decoder_3x8_1_s7), .in_1(in_4));
  nor nor_1 (Overflow_2, decoder_3x8_1_s7, decoder_3x8_1_s6, out_6[0], out_6[1], out_6[2], out_6[3]);
  BUFFER buffer_1 (.in_2(decoder_3x8_1_s0), .B(B), .S(out_6));
  AD_4 ad_4_1 (.in_2(A), .out_4(ad_4_1_out_4), .in_1(B), .in_3(1'b0), .out_5(ad_4_1_out_5));
  BUFFER buffer_2 (.in_2(decoder_3x8_1_s1), .B(ad_4_1_out_5), .S(out_6));
  SUB_4 sub_4_1 (.in_2(A), .out_4(sub_4_1_out_4), .in_1(B), .in_3(1'b0), .out_5(sub_4_1_out_5));
  BUFFER buffer_3 (.in_2(decoder_3x8_1_s2), .B(sub_4_1_out_5), .S(out_6));
  OR or_2 (.A(A), .B(B), .S(or_2_s));
  BUFFER buffer_4 (.in_2(decoder_3x8_1_s3), .B(or_2_s), .S(out_6));
  BUFFER_CONTROLADO_INVERTIDO buffer_controlado_invertido_1 (.in_2(decoder_3x8_1_s4), .S(out_6), .B(B));
  ROT_W rot_w_1 (.abcd_2(rot_w_1_abcd_2), .ABCD(A), .XY(B[1:0]));
  ROT_L rot_l_1 (.abcd_2(rot_l_1_abcd_2), .ABCD(A), .XY(B[1:0]));
  not not_1 (not_1_out, D);
  BUFFER buffer_5 (.in_2(D), .B(rot_w_1_abcd_2), .S(buffer_5_s));
  BUFFER buffer_6 (.in_2(not_1_out), .B(rot_l_1_abcd_2), .S(buffer_5_s));
  BUFFER buffer_7 (.in_2(decoder_3x8_1_s5), .B(buffer_5_s), .S(out_6));
endmodule

module REG_AC (
  input  Clock,
  input  [3:0] D,
  output [3:0] D_2
);

  D_Flip_Flop d_ff_1 (.clk(Clock), .D(D[3]), .Q(D_2[3]));  // open: Qn, preset, en, reset
  D_Flip_Flop d_ff_2 (.clk(Clock), .D(D[2]), .Q(D_2[2]));  // open: Qn, preset, en, reset
  D_Flip_Flop d_ff_3 (.clk(Clock), .D(D[1]), .Q(D_2[1]));  // open: Qn, preset, en, reset
  D_Flip_Flop d_ff_4 (.clk(Clock), .D(D[0]), .Q(D_2[0]));  // open: Qn, preset, en, reset
endmodule

module MUX (
  input  [3:0] E,
  input  [3:0] D,
  input  in_3,
  output [3:0] S
);

  wire not_1_out;

  BUFFER buffer_1 (.in_2(not_1_out), .B(E), .S(S));
  not not_1 (not_1_out, in_3);
  BUFFER buffer_2 (.in_2(in_3), .B(D), .S(S));
endmodule

module IR (
  input  Clock,
  input  [7:0] D,
  output [7:0] Q
);

  D_Flip_Flop #(.trigger("falling")) D3 (.clk(Clock), .D(D[7]), .Q(Q[7]));  // open: Qn, preset, en, reset
  D_Flip_Flop #(.trigger("falling")) D2 (.clk(Clock), .D(D[6]), .Q(Q[6]));  // open: Qn, preset, en, reset
  D_Flip_Flop #(.trigger("falling")) D1 (.clk(Clock), .D(D[5]), .Q(Q[5]));  // open: Qn, preset, en, reset
  D_Flip_Flop #(.trigger("falling")) D0 (.clk(Clock), .D(D[4]), .Q(Q[4]));  // open: Qn, preset, en, reset
  D_Flip_Flop #(.trigger("falling")) D3_2 (.clk(Clock), .D(D[3]), .Q(Q[3]));  // open: Qn, preset, en, reset
  D_Flip_Flop #(.trigger("falling")) D2_2 (.clk(Clock), .D(D[2]), .Q(Q[2]));  // open: Qn, preset, en, reset
  D_Flip_Flop #(.trigger("falling")) D1_2 (.clk(Clock), .D(D[1]), .Q(Q[1]));  // open: Qn, preset, en, reset
  D_Flip_Flop #(.trigger("falling")) D0_2 (.clk(Clock), .D(D[0]), .Q(Q[0]));  // open: Qn, preset, en, reset
endmodule

module UC (
  input  [7:0] \Instrução ,
  input  Clock,
  input  Reset,
  input  Overflow,
  input  Zero,
  output [3:0] Dados,
  output [3:0] \Barr__Endereços ,
  output [3:0] Operando,
  output clk_Rl,
  output clk_PC,
  output clk_AC,
  output clk_RAM,
  output Rst_PC,
  output \Direção ,
  output E,
  output [2:0] \Operação ,
  output R_W,
  output Load
);

  wire GoTo_out, JPO_out, JPZ_out, nand_1_out;
  wire [1:0] counter_1_q;

  Counter #(.width(2), .max('h3)) counter_1 (.Q(counter_1_q), .clk(Clock), .clr(Reset));  // open: load, D, count, carry
  nand Storage (R_W, \Instrução [7], \Instrução [6], \Instrução [5], \Instrução [4], clk_AC);
  and GoTo (GoTo_out, \Instrução [7], \Instrução [6], \Instrução [5], ~\Instrução [4], clk_PC);  // AND_Gate
  and and_1 (clk_Rl, ~counter_1_q[0], ~counter_1_q[1]);  // AND_Gate
  and JPO (JPO_out, \Instrução [7], \Instrução [6], ~\Instrução [5], \Instrução [4], clk_PC, Overflow);  // AND_Gate
  or or_1 (Load, GoTo_out, JPO_out, JPZ_out);
  and and_2 (clk_PC, counter_1_q[0], ~counter_1_q[1]);  // AND_Gate
  and JPZ (JPZ_out, \Instrução [7], \Instrução [6], ~\Instrução [5], ~\Instrução [4], clk_PC, Zero);  // AND_Gate
  and and_3 (clk_AC, ~counter_1_q[0], counter_1_q[1]);  // AND_Gate
  and and_4 (clk_RAM, counter_1_q[0], counter_1_q[1]);
  nand nand_1 (nand_1_out, \Instrução [7], ~\Instrução [6], \Instrução [5]);  // NAND_Gate
  and and_5 (E, \Instrução [4], nand_1_out);

  assign \Barr__Endereços  = \Instrução [3:0];
  assign Dados = \Instrução [3:0];
  assign \Direção  = \Instrução [4];
  assign Operando = \Instrução [3:0];
  assign \Operação  = \Instrução [7:5];
  assign Rst_PC = Reset;
endmodule
